// Logisim project 2-bit SYNCHRONOUS COUNTER.circ as structural Verilog: 1 circuit, main circuit main
module main (
  input  in_1,
  output out_2,
  output out_3
);

  wire d_ff_1_qn, d_ff_2_qn, xor_1_out;

  D_Flip_Flop d_ff_1 (.clk(in_1), .D(xor_1_out), .Q(out_3), .Qn(d_ff_1_qn));  // open: preset, en, reset
  D_Flip_Flop d_ff_2 (.clk(in_1), .D(d_ff_2_qn), .Q(out_2), .Qn(d_ff_2_qn));  // open: preset, en, reset
  xor xor_1 (xor_1_out, d_ff_1_qn, d_ff_2_qn);
endmodule
