// Logisim project 3-bit ASYNCHRONOUS COUNTER.circ as structural Verilog: 1 circuit, main circuit main
module main (
  input  clk,
  input  clk_2,
  output z,
  output x,
  output y,
  output out_6,
  output x_2,
  output y_2
);

  wire d_ff_1_qn, d_ff_2_qn, d_ff_3_qn, d_ff_4_qn, d_ff_5_qn, d_ff_6_qn, not_1_out;

  not not_1 (not_1_out, clk);
  D_Flip_Flop d_ff_1 (.clk(d_ff_3_qn), .D(d_ff_1_qn), .Q(x), .Qn(d_ff_1_qn));  // open: preset, en, reset
  D_Flip_Flop d_ff_2 (.clk(d_ff_4_qn), .D(d_ff_2_qn), .Q(x_2), .Qn(d_ff_2_qn));  // open: preset, en, reset
  D_Flip_Flop d_ff_3 (.clk(d_ff_5_qn), .D(d_ff_3_qn), .Q(y), .Qn(d_ff_3_qn));  // open: preset, en, reset
  D_Flip_Flop d_ff_4 (.clk(d_ff_6_qn), .D(d_ff_4_qn), .Q(y_2), .Qn(d_ff_4_qn));  // open: preset, en, reset
  D_Flip_Flop d_ff_5 (.clk(not_1_out), .D(d_ff_5_qn), .Q(z), .Qn(d_ff_5_qn));  // open: preset, en, reset
  D_Flip_Flop d_ff_6 (.clk(clk_2), .D(d_ff_6_qn), .Q(out_6), .Qn(d_ff_6_qn));  // open: preset, en, reset

  // Notes on the sheet:
  //   with inverted clock
  //   without inverted clock
endmodule
