// Logisim project 4-bit SYNCHRONOUS COUNTER.circ as structural Verilog: 1 circuit, main circuit main
module main (
  input  clk,
  output w,
  output x,
  output y,
  output z
);

  wire and_1_out, and_2_out, d_ff_1_qn, xor_1_out, xor_2_out, xor_3_out;

  xor xor_1 (xor_1_out, w, x);
  and and_1 (and_1_out, x, w);
  and and_2 (and_2_out, y, x, w);
  xor xor_2 (xor_2_out, and_1_out, y);
  xor xor_3 (xor_3_out, and_2_out, z);
  D_Flip_Flop d_ff_1 (.clk(clk), .D(d_ff_1_qn), .Q(w), .Qn(d_ff_1_qn));  // open: preset, en, reset
  D_Flip_Flop d_ff_2 (.clk(clk), .D(xor_1_out), .Q(x));  // open: Qn, preset, en, reset
  D_Flip_Flop d_ff_3 (.clk(clk), .D(xor_2_out), .Q(y));  // open: Qn, preset, en, reset
  D_Flip_Flop d_ff_4 (.clk(clk), .D(xor_3_out), .Q(z));  // open: Qn, preset, en, reset
endmodule
